// Logisim project jrmips.circ as structural Verilog: 12 circuits, main circuit main
module main (
);

  wire clock_1_out, decoder2_1_branch, decoder2_1_halt, decoder2_1_jump, decoder2_1_memread,
       decoder2_1_memtoreg, decoder2_1_memwrite, decoder2_1_put, decoder2_1_regwrite, decoder2_1_shift,
       inputsplit_1_func, not_1_out, or_1_out, pc_mod_1_jal;
  wire [1:0] decoder2_1_aluop;
  wire [2:0] inputsplit_1_rs, inputsplit_1_rt;
  wire [3:0] inputsplit_1_opcode, inputsplit_1_shamt;
  wire [7:0] adder_1_out, controlled_buffer_1_out, inputsplit_1_imm, pc_mod_1_output, PC_q;
  wire [15:0] alu_1_result, alu_source_1_output, bit_extender_1_out, demultiplexer_1_out0,
       demultiplexer_1_out1, multiplexer_1_out, multiplexer_2_out, multiplexer_3_out, multiplexer_4_out,
       ram_1_data, register_1_q, registers_1_read_out1, registers_1_read_out2, rom_1_data;

  LED led_1 (.in(decoder2_1_halt));
  Clock clock_1 (.out(clock_1_out));
  Register PC (.D(pc_mod_1_output), .en(not_1_out), .Q(PC_q), .clk(clock_1_out));  // open: clr
  not not_1 (not_1_out, decoder2_1_halt);
  PC_Mod pc_mod_1 (
    .Jump(decoder2_1_jump), .Branch(decoder2_1_branch), .OpCode(inputsplit_1_opcode),
    .Rs(registers_1_read_out1), .Immed(inputsplit_1_imm), .PC_1(adder_1_out), .jal(pc_mod_1_jal),
    .Output(pc_mod_1_output));
  Adder adder_1 (.a(PC_q), .b(8'h1), .out(adder_1_out));  // open: cin, cout
  Decoder2 decoder2_1 (
    .OpCode(inputsplit_1_opcode), .SubOp(inputsplit_1_func), .MemWrite(decoder2_1_memwrite),
    .MemRead(decoder2_1_memread), .ALUOp(decoder2_1_aluop), .RegWrite(decoder2_1_regwrite),
    .MemToReg(decoder2_1_memtoreg), .Branch(decoder2_1_branch), .Shift(decoder2_1_shift),
    .Jump(decoder2_1_jump), .Put(decoder2_1_put), .Halt(decoder2_1_halt));
  assign bit_extender_1_out = {{8{1'b0}}, adder_1_out};  // Bit_Extender bit_extender_1
  InputSplit inputsplit_1 (
    .Instruction(rom_1_data), .OpCode(inputsplit_1_opcode), .Rs(inputsplit_1_rs), .Rt(inputsplit_1_rt),
    .Shamt(inputsplit_1_shamt), .Func(inputsplit_1_func), .Imm(inputsplit_1_imm));
  ROM #(.dataWidth(16)) rom_1 (.addr(PC_q), .data(rom_1_data));  // open: sel
  ALU_Source alu_source_1 (
    .func(inputsplit_1_func), .OpCode(inputsplit_1_opcode), .Immed(inputsplit_1_imm),
    .Shamt(inputsplit_1_shamt), .Rt(multiplexer_2_out), .Output(alu_source_1_output));
  Registers registers_1 (
    .Read_In1(inputsplit_1_rs), .Write_Inst(decoder2_1_regwrite), .Write_Data(multiplexer_1_out),
    .Read_In2(inputsplit_1_rt), .Read_Out1(registers_1_read_out1), .Read_Out2(registers_1_read_out2),
    .Clock(clock_1_out));
  Multiplexer #(.width(16), .enable("false")) multiplexer_1 (
    .in0(multiplexer_3_out), .in1(bit_extender_1_out), .out(multiplexer_1_out), .sel(pc_mod_1_jal));
  Multiplexer #(.width(16)) multiplexer_2 (
    .in0(registers_1_read_out2), .in1(registers_1_read_out1), .out(multiplexer_2_out), .sel(decoder2_1_shift));  // open: en
  or or_1 (or_1_out, decoder2_1_memwrite, decoder2_1_memread);
  Multiplexer #(.width(16)) multiplexer_3 (
    .in0(multiplexer_4_out), .in1(demultiplexer_1_out1), .out(multiplexer_3_out), .sel(decoder2_1_shift));  // open: en
  Demultiplexer #(.width(16), .enable("false")) demultiplexer_1 (
    .out0(demultiplexer_1_out0), .out1(demultiplexer_1_out1), .in(alu_source_1_output), .sel(decoder2_1_shift));
  ALU alu_1 (.A(registers_1_read_out1), .B(demultiplexer_1_out0), .Op(decoder2_1_aluop), .Result(alu_1_result));
  assign controlled_buffer_1_out = or_1_out ? registers_1_read_out2[7:0] : 8'bz;  // Controlled_Buffer controlled_buffer_1
  Multiplexer #(.width(16)) multiplexer_4 (
    .in0(alu_1_result), .in1(ram_1_data), .out(multiplexer_4_out), .sel(decoder2_1_memtoreg));  // open: en
  Hex_Digit_Display hex_digit_display_1 (.value(register_1_q[11:8]));  // open: dp
  Hex_Digit_Display hex_digit_display_2 (.value(register_1_q[15:12]));  // open: dp
  Register #(.width(16), .trigger("falling")) register_1 (
    .D(registers_1_read_out1), .en(decoder2_1_put), .Q(register_1_q), .clk(clock_1_out));  // open: clr
  Hex_Digit_Display hex_digit_display_3 (.value(register_1_q[3:0]));  // open: dp
  Hex_Digit_Display hex_digit_display_4 (.value(register_1_q[7:4]));  // open: dp
  RAM #(.dataWidth(16), .bus("separate")) ram_1 (
    .addr(controlled_buffer_1_out), .din(registers_1_read_out1), .data(ram_1_data),
    .str(decoder2_1_memwrite), .clk(clock_1_out), .ld(decoder2_1_memread));  // open: sel, clr

  // Notes on the sheet:
  //   Addison Beall
  //   aeb95@pitt.edu
  //   contents of rom_1 (hex, n*v repeats v):
  //   23ff 200 13c0 3c0 2e4a e00 2b64 a00 1540 400 1a81 a00 35c0 400 3541 400 4e08 e00 4e07 e00 7e81 7080
  //   a00 a01
endmodule

module ALU (
  input  [1:0] Op,
  input  [15:0] A,
  input  [15:0] B,
  output [15:0] Result
);

  wire [15:0] adder_1_out, and_1_out, nor_1_out, subtractor_1_out;

  assign and_1_out = A & B;  // AND_Gate and_1, 16 bits wide
  assign nor_1_out = ~(A | B);  // NOR_Gate nor_1, 16 bits wide
  Adder #(.width(16)) adder_1 (.a(A), .b(B), .out(adder_1_out), .cin(1'b0));  // open: cout
  Subtractor #(.width(16)) subtractor_1 (.a(A), .b(B), .out(subtractor_1_out), .bin(1'b0));  // open: bout
  Multiplexer #(.select(2), .width(16), .enable("false")) multiplexer_1 (
    .in0(and_1_out), .in1(nor_1_out), .in2(adder_1_out), .in3(subtractor_1_out), .out(Result), .sel(Op));
endmodule

module Registers (
  input  [2:0] Read_In1,
  input  Write_Inst,
  input  [15:0] Write_Data,
  input  [2:0] Read_In2,
  input  Clock,
  output [15:0] Read_Out1,
  output [15:0] Read_Out2
);

  wire demultiplexer_1_out0, demultiplexer_1_out1, demultiplexer_1_out2, demultiplexer_1_out3,
       demultiplexer_1_out4, demultiplexer_1_out5, demultiplexer_1_out6, demultiplexer_1_out7;
  wire [15:0] r0_q, r1_q, r2_q, r3_q, r4_q, r5_q, r6_q, r7_q;

  Demultiplexer #(.select(3)) demultiplexer_1 (
    .out0(demultiplexer_1_out0), .out1(demultiplexer_1_out1), .out2(demultiplexer_1_out2),
    .out3(demultiplexer_1_out3), .out4(demultiplexer_1_out4), .out5(demultiplexer_1_out5),
    .out6(demultiplexer_1_out6), .out7(demultiplexer_1_out7), .in(Write_Inst), .sel(Read_In1));  // open: en
  Register #(.width(16)) r0 (.D(Write_Data), .en(demultiplexer_1_out0), .Q(r0_q), .clk(Clock));  // open: clr
  Register #(.width(16)) r7 (.D(Write_Data), .en(demultiplexer_1_out7), .Q(r7_q), .clk(Clock));  // open: clr
  Register #(.width(16)) r1 (.D(Write_Data), .en(demultiplexer_1_out1), .Q(r1_q), .clk(Clock));  // open: clr
  Register #(.width(16)) r6 (.D(Write_Data), .en(demultiplexer_1_out6), .Q(r6_q), .clk(Clock));  // open: clr
  Register #(.width(16)) r2 (.D(Write_Data), .en(demultiplexer_1_out2), .Q(r2_q), .clk(Clock));  // open: clr
  Register #(.width(16)) r5 (.D(Write_Data), .en(demultiplexer_1_out5), .Q(r5_q), .clk(Clock));  // open: clr
  Register #(.width(16)) r3 (.D(Write_Data), .en(demultiplexer_1_out3), .Q(r3_q), .clk(Clock));  // open: clr
  Register #(.width(16)) r4 (.D(Write_Data), .en(demultiplexer_1_out4), .Q(r4_q), .clk(Clock));  // open: clr
  Multiplexer #(.select(3), .width(16), .enable("false")) multiplexer_1 (
    .in0(r0_q), .in1(r1_q), .in2(r2_q), .in3(r3_q), .in4(r4_q), .in5(r5_q), .in6(r6_q), .in7(r7_q),
    .out(Read_Out1), .sel(Read_In1));
  Multiplexer #(.select(3), .width(16), .enable("false")) multiplexer_2 (
    .in0(r0_q), .in1(r1_q), .in2(r2_q), .in3(r3_q), .in4(r4_q), .in5(r5_q), .in6(r6_q), .in7(r7_q),
    .out(Read_Out2), .sel(Read_In2));
endmodule

module Decoder (
  input  [3:0] Clock,
  input  Func,
  output jump,
  output shift,
  output halt,
  output branch,
  output put,
  output memtoreg,
  output regwrite,
  output ALUSrc,
  output [1:0] ALUOp,
  output Memwrite,
  output Memread
);

  wire and_1_out, and_2_out, and_3_out, and_4_out, and_8_out, and_9_out, and_10_out, and_11_out, and_12_out,
       and_13_out, and_14_out, and_15_out, and_16_out, and_17_out, and_18_out, and_19_out, and_20_out,
       not_1_out, not_2_out, not_3_out, not_4_out, not_5_out, not_6_out, not_7_out, not_8_out, not_9_out,
       not_10_out, not_11_out, not_12_out, not_13_out, not_14_out, not_15_out, not_16_out, not_17_out,
       not_18_out, not_19_out, not_20_out, not_21_out, not_22_out, not_23_out, not_24_out, not_25_out,
       not_26_out, not_27_out, not_28_out, not_29_out, not_30_out, not_31_out, not_32_out, not_33_out,
       not_34_out, not_35_out, not_36_out, not_37_out, not_38_out, not_39_out, not_40_out, not_41_out,
       not_42_out, not_43_out;

  not not_1 (not_1_out, Clock[2]);
  not not_2 (not_2_out, Clock[3]);
  not not_3 (not_3_out, Clock[0]);
  not not_4 (not_4_out, Clock[1]);
  not not_5 (not_5_out, Clock[0]);
  not not_6 (not_6_out, Clock[2]);
  not not_7 (not_7_out, Clock[3]);
  not not_8 (not_8_out, Clock[3]);
  not not_9 (not_9_out, Clock[1]);
  not not_10 (not_10_out, Clock[0]);
  not not_11 (not_11_out, Clock[1]);
  not not_12 (not_12_out, Clock[3]);
  not not_13 (not_13_out, Clock[2]);
  not not_14 (not_14_out, Clock[1]);
  not not_15 (not_15_out, Clock[3]);
  not not_16 (not_16_out, Clock[0]);
  not not_17 (not_17_out, Clock[2]);
  not not_18 (not_18_out, Clock[3]);
  not not_19 (not_19_out, Clock[3]);
  not not_20 (not_20_out, Clock[1]);
  not not_21 (not_21_out, Clock[0]);
  not not_22 (not_22_out, Clock[2]);
  not not_23 (not_23_out, Clock[3]);
  not not_24 (not_24_out, Func);
  not not_25 (not_25_out, Clock[0]);
  not not_26 (not_26_out, Clock[3]);
  not not_27 (not_27_out, Func);
  not not_28 (not_28_out, Clock[3]);
  not not_29 (not_29_out, Clock[0]);
  not not_30 (not_30_out, Clock[2]);
  not not_31 (not_31_out, Clock[0]);
  not not_32 (not_32_out, Clock[2]);
  not not_33 (not_33_out, Func);
  and and_1 (and_1_out, Clock[0], Clock[1], not_1_out);
  and and_2 (and_2_out, Clock[0], Clock[1], not_2_out);
  and and_3 (and_3_out, not_3_out, not_4_out, Clock[2], Clock[3]);
  and and_4 (and_4_out, not_5_out, Clock[1], not_6_out, not_7_out);
  and and_5 (halt, Clock[1], Clock[2], not_8_out);
  and and_6 (branch, Clock[0], not_9_out);
  and and_7 (put, not_10_out, Clock[1], Clock[2], Clock[3]);
  or or_1 (memtoreg, not_11_out, not_12_out, Func, Clock[2], Clock[0]);
  not not_34 (not_34_out, Clock[0]);
  and and_8 (and_8_out, not_34_out, not_35_out);
  not not_35 (not_35_out, Clock[1]);
  not not_36 (not_36_out, Clock[0]);
  not not_37 (not_37_out, Clock[2]);
  and and_9 (and_9_out, not_36_out, not_37_out, not_38_out);
  not not_38 (not_38_out, Clock[3]);
  not not_39 (not_39_out, Clock[0]);
  and and_10 (and_10_out, not_39_out, not_40_out, not_41_out);
  not not_40 (not_40_out, Clock[2]);
  not not_41 (not_41_out, Func);
  and and_11 (and_11_out, Clock[0], Clock[1], not_13_out, Clock[3]);
  and and_12 (and_12_out, not_14_out, Clock[2], not_15_out);
  and and_13 (and_13_out, not_16_out, not_17_out, not_18_out);
  and and_14 (and_14_out, Clock[1], Clock[2], not_19_out);
  and and_15 (and_15_out, Clock[0], not_20_out, Clock[2]);
  and and_16 (and_16_out, not_21_out, not_22_out, not_23_out, not_24_out);
  not not_42 (not_42_out, Clock[0]);
  and and_17 (and_17_out, not_42_out, Clock[3], Func);
  and and_18 (and_18_out, not_25_out, Clock[1], not_26_out, not_27_out);
  not not_43 (not_43_out, Clock[1]);
  and and_19 (and_19_out, Clock[0], not_43_out, Clock[3]);
  and and_20 (and_20_out, Clock[0], Clock[1], Clock[2], not_28_out);
  and and_21 (Memwrite, not_29_out, Clock[1], not_30_out, Clock[3], Func);
  and and_22 (Memread, not_31_out, Clock[1], not_32_out, Clock[3], not_33_out);
  or or_2 (jump, and_1_out, and_2_out);
  or or_3 (shift, and_3_out, and_4_out);
  or or_4 (regwrite, and_8_out, and_9_out, and_10_out, and_11_out);
  or or_5 (ALUSrc, and_12_out, Clock[0]);
  or or_6 (ALUOp[0], and_13_out, and_14_out, and_15_out);
  or or_7 (ALUOp[1], and_16_out, and_17_out, and_18_out, and_19_out, and_20_out);
endmodule

// Branch Com
module Branch_Comparator (
  input  [15:0] Input,
  input  OpCode,
  input  Enable,
  output Equal
);

  wire comparator_1_eq, not_1_out;

  Comparator #(.width(16)) comparator_1 (.a(Input), .b({16{1'b0}}), .eq(comparator_1_eq));  // open: gt, lt
  not not_1 (not_1_out, comparator_1_eq);
  Multiplexer multiplexer_1 (.in0(not_1_out), .in1(comparator_1_eq), .out(Equal), .sel(OpCode), .en(Enable));
endmodule

module InputSplit (
  input  [15:0] Instruction,
  output [3:0] OpCode,
  output [2:0] Rs,
  output [2:0] Rt,
  output [3:0] Shamt,
  output Func,
  output [7:0] Imm
);


  assign Func = Instruction[0];
  assign Imm = Instruction[8:1];
  assign OpCode = Instruction[15:12];
  assign Rs = Instruction[11:9];
  assign Rt = Instruction[8:6];
  assign Shamt = Instruction[4:1];
endmodule

module Signer (
  input  Func,
  input  [7:0] Unsigned,
  output [15:0] Signed
);

  wire [15:0] bit_extender_1_out, bit_extender_2_out;

  assign bit_extender_1_out = {{8{Unsigned[7]}}, Unsigned};  // Bit_Extender bit_extender_1
  assign bit_extender_2_out = {{8{1'b0}}, Unsigned};  // Bit_Extender bit_extender_2
  Multiplexer #(.width(16)) multiplexer_1 (
    .in0(bit_extender_1_out), .in1(bit_extender_2_out), .out(Signed), .sel(Func));  // open: en
endmodule

module Shift (
  input  func,
  input  [15:0] Reg_In,
  input  [3:0] Shamt,
  output [15:0] Shifted
);

  wire [15:0] shifter_1_out, shifter_2_out;

  Shifter #(.width(16)) shifter_1 (.in(Reg_In), .\dist (Shamt), .out(shifter_1_out));
  Shifter #(.width(16), .shift("lr")) shifter_2 (.in(Reg_In), .\dist (Shamt), .out(shifter_2_out));
  Multiplexer #(.width(16)) multiplexer_1 (
    .in0(shifter_1_out), .in1(shifter_2_out), .out(Shifted), .sel(func));  // open: en
endmodule

// Decoder
module Decoder2 (
  input  [3:0] OpCode,
  input  SubOp,
  output MemWrite,
  output MemRead,
  output [1:0] ALUOp,
  output RegWrite,
  output MemToReg,
  output Branch,
  output Shift,
  output Jump,
  output Put,
  output Halt
);

  wire and_3_out, and_4_out, and_5_out, and_6_out, and_7_out, and_8_out, and_9_out, and_10_out, and_11_out,
       and_12_out, and_13_out, and_14_out, and_15_out, and_16_out, and_17_out, and_18_out, and_21_out,
       and_22_out, not_1_out, not_2_out, not_3_out, not_4_out, not_5_out, not_6_out, not_7_out, not_8_out,
       not_9_out, not_10_out, not_11_out, not_12_out, not_13_out, not_14_out, not_15_out, not_16_out,
       not_17_out, not_18_out, not_19_out, not_20_out, not_21_out, not_22_out, not_23_out, not_24_out,
       not_25_out, not_26_out, not_27_out, not_28_out, not_29_out, not_30_out, not_31_out, not_32_out,
       not_33_out, not_34_out, not_35_out, not_36_out, not_37_out, not_38_out, not_39_out;

  not not_1 (not_1_out, OpCode[3]);
  not not_2 (not_2_out, OpCode[3]);
  not not_3 (not_3_out, SubOp);
  not not_4 (not_4_out, OpCode[3]);
  not not_5 (not_5_out, OpCode[2]);
  not not_6 (not_6_out, OpCode[0]);
  not not_7 (not_7_out, OpCode[3]);
  not not_8 (not_8_out, OpCode[1]);
  not not_9 (not_9_out, OpCode[2]);
  not not_10 (not_10_out, OpCode[1]);
  not not_11 (not_11_out, OpCode[2]);
  not not_12 (not_12_out, OpCode[1]);
  not not_13 (not_13_out, OpCode[0]);
  not not_14 (not_14_out, SubOp);
  not not_15 (not_15_out, OpCode[3]);
  not not_16 (not_16_out, SubOp);
  not not_17 (not_17_out, OpCode[0]);
  not not_18 (not_18_out, SubOp);
  not not_19 (not_19_out, OpCode[2]);
  not not_20 (not_20_out, OpCode[1]);
  not not_21 (not_21_out, OpCode[3]);
  not not_22 (not_22_out, OpCode[1]);
  not not_23 (not_23_out, OpCode[0]);
  not not_24 (not_24_out, OpCode[2]);
  not not_25 (not_25_out, OpCode[1]);
  not not_26 (not_26_out, OpCode[0]);
  not not_27 (not_27_out, OpCode[1]);
  not not_28 (not_28_out, OpCode[2]);
  not not_29 (not_29_out, OpCode[3]);
  and and_1 (MemWrite, not_1_out, OpCode[2], OpCode[1], SubOp);
  and and_2 (MemRead, not_2_out, OpCode[2], OpCode[1], not_3_out);
  and and_3 (and_3_out, not_4_out, not_5_out, not_6_out);
  and and_4 (and_4_out, not_7_out, not_8_out);
  and and_5 (and_5_out, OpCode[3], OpCode[2], OpCode[1], OpCode[0]);
  and and_6 (and_6_out, not_9_out, OpCode[0], SubOp);
  and and_7 (and_7_out, not_10_out, OpCode[0], SubOp);
  and and_8 (and_8_out, OpCode[3], not_11_out);
  and and_9 (and_9_out, OpCode[3], not_12_out);
  not not_30 (not_30_out, OpCode[3]);
  and and_10 (and_10_out, not_30_out, not_31_out, OpCode[0]);
  not not_31 (not_31_out, OpCode[2]);
  not not_32 (not_32_out, OpCode[3]);
  not not_33 (not_33_out, OpCode[2]);
  and and_11 (and_11_out, not_32_out, not_33_out, OpCode[1]);
  not not_34 (not_34_out, OpCode[2]);
  and and_12 (and_12_out, not_34_out, OpCode[1], OpCode[0]);
  not not_35 (not_35_out, OpCode[3]);
  and and_13 (and_13_out, not_35_out, OpCode[2], not_36_out);
  not not_36 (not_36_out, OpCode[1]);
  not not_37 (not_37_out, OpCode[3]);
  and and_14 (and_14_out, not_37_out, OpCode[2], not_38_out);
  not not_38 (not_38_out, SubOp);
  and and_15 (and_15_out, OpCode[2], not_39_out, OpCode[0]);
  not not_39 (not_39_out, OpCode[1]);
  and and_16 (and_16_out, OpCode[2], OpCode[1], not_13_out, not_14_out);
  and and_17 (and_17_out, not_15_out, OpCode[2], OpCode[1], not_16_out);
  and and_18 (and_18_out, OpCode[2], OpCode[1], not_17_out, not_18_out);
  and and_19 (Branch, OpCode[3], not_19_out, not_20_out);
  and and_20 (Shift, not_21_out, OpCode[2], not_22_out, not_23_out);
  and and_21 (and_21_out, OpCode[3], not_24_out, OpCode[1]);
  and and_22 (and_22_out, OpCode[3], OpCode[2], not_25_out);
  and and_23 (Put, not_26_out, not_27_out, not_28_out, not_29_out);
  and and_24 (Halt, OpCode[3], OpCode[2], OpCode[1], OpCode[0]);
  or or_1 (ALUOp[1], and_3_out, and_4_out, and_5_out);
  or or_2 (ALUOp[0], and_6_out, and_7_out, and_8_out, and_9_out);
  or or_3 (MemToReg, and_17_out, and_18_out);
  or or_4 (Jump, and_21_out, and_22_out);
  or or_5 (RegWrite, and_10_out, and_11_out, and_12_out, and_13_out, and_14_out, and_15_out, and_16_out);
endmodule

module Decoder4 (
  input  Op3,
  input  Op2,
  input  Op1,
  input  Op0,
  input  SubOp,
  output MemWrite,
  output MemRead,
  output RegWrite,
  output MemToReg,
  output Branch,
  output Shift,
  output Jump,
  output Put,
  output Halt
);

  wire and_4_out, and_5_out, and_6_out, and_7_out, and_8_out, and_9_out, and_10_out, and_11_out, and_12_out,
       and_13_out, and_14_out, and_15_out, and_16_out, and_17_out, and_18_out, and_19_out, and_22_out,
       and_23_out, not_1_out, not_2_out, not_3_out, not_4_out, not_5_out, not_6_out, not_7_out, not_8_out,
       not_9_out, not_10_out, not_11_out, not_12_out, not_13_out, not_14_out, not_15_out, not_16_out,
       not_17_out, not_18_out, not_19_out, not_20_out, not_21_out, not_22_out, not_23_out, not_24_out,
       not_25_out, not_26_out, not_27_out, not_28_out, not_29_out, not_30_out, not_31_out, not_32_out,
       not_33_out, not_34_out, not_35_out, not_36_out, not_37_out, not_38_out, not_39_out, or_1_out, or_2_out;

  not not_1 (not_1_out, Op3);
  not not_2 (not_2_out, Op3);
  not not_3 (not_3_out, SubOp);
  not not_4 (not_4_out, Op3);
  not not_5 (not_5_out, Op2);
  not not_6 (not_6_out, Op0);
  not not_7 (not_7_out, Op3);
  not not_8 (not_8_out, Op1);
  not not_9 (not_9_out, Op2);
  not not_10 (not_10_out, Op1);
  not not_11 (not_11_out, Op2);
  not not_12 (not_12_out, Op1);
  not not_13 (not_13_out, Op3);
  not not_14 (not_14_out, Op2);
  not not_15 (not_15_out, Op3);
  not not_16 (not_16_out, Op2);
  not not_17 (not_17_out, Op2);
  not not_18 (not_18_out, Op3);
  not not_19 (not_19_out, Op1);
  not not_20 (not_20_out, Op3);
  not not_21 (not_21_out, SubOp);
  not not_22 (not_22_out, Op1);
  not not_23 (not_23_out, Op0);
  not not_24 (not_24_out, SubOp);
  not not_25 (not_25_out, Op3);
  not not_26 (not_26_out, SubOp);
  not not_27 (not_27_out, Op0);
  not not_28 (not_28_out, SubOp);
  not not_29 (not_29_out, Op2);
  not not_30 (not_30_out, Op1);
  not not_31 (not_31_out, Op3);
  not not_32 (not_32_out, Op1);
  not not_33 (not_33_out, Op0);
  not not_34 (not_34_out, Op2);
  not not_35 (not_35_out, Op1);
  not not_36 (not_36_out, Op0);
  not not_37 (not_37_out, Op1);
  not not_38 (not_38_out, Op2);
  not not_39 (not_39_out, Op3);
  and and_1 (Halt, Op3, Op2, Op1, Op0);
  and and_2 (MemWrite, not_1_out, Op2, Op1, SubOp);
  and and_3 (MemRead, not_2_out, Op2, Op1, not_3_out);
  and and_4 (and_4_out, not_4_out, not_5_out, not_6_out);
  and and_5 (and_5_out, not_7_out, not_8_out);
  and and_6 (and_6_out, Op3, Op2, Op1, Op0);
  and and_7 (and_7_out, not_9_out, Op0, SubOp);
  and and_8 (and_8_out, not_10_out, Op0, SubOp);
  and and_9 (and_9_out, Op3, not_11_out);
  and and_10 (and_10_out, Op3, not_12_out);
  and and_11 (and_11_out, not_13_out, not_14_out, Op0);
  and and_12 (and_12_out, not_15_out, not_16_out, Op1);
  and and_13 (and_13_out, not_17_out, Op1, Op0);
  and and_14 (and_14_out, not_18_out, Op2, not_19_out);
  and and_15 (and_15_out, not_20_out, Op2, not_21_out);
  and and_16 (and_16_out, Op2, not_22_out, Op0);
  and and_17 (and_17_out, Op2, Op1, not_23_out, not_24_out);
  and and_18 (and_18_out, not_25_out, Op2, Op1, not_26_out);
  and and_19 (and_19_out, Op2, Op1, not_27_out, not_28_out);
  and and_20 (Branch, Op3, not_29_out, not_30_out);
  and and_21 (Shift, not_31_out, Op2, not_32_out, not_33_out);
  and and_22 (and_22_out, Op3, not_34_out, Op1);
  and and_23 (and_23_out, Op3, Op2, not_35_out);
  and and_24 (Put, not_36_out, not_37_out, not_38_out, not_39_out);
  or or_1 (or_1_out, and_4_out, and_5_out, and_6_out);
  or or_2 (or_2_out, and_7_out, and_8_out, and_9_out, and_10_out);
  or or_3 (RegWrite, and_11_out, and_12_out, and_13_out, and_14_out, and_15_out, and_16_out, and_17_out);
  or or_4 (MemToReg, and_18_out, and_19_out);
  or or_5 (Jump, and_22_out, and_23_out);
endmodule

module PC_Mod (
  input  Jump,
  input  Branch,
  input  [3:0] OpCode,
  input  [15:0] Rs,
  input  [7:0] Immed,
  input  [7:0] PC_1,
  output jal,
  output [7:0] Output
);

  wire branch_comparator_1_equal, not_1_out, or_1_out;
  wire [7:0] multiplexer_1_out, multiplexer_2_out;

  or or_1 (or_1_out, Jump, Branch);
  Branch_Comparator branch_comparator_1 (
    .Input(Rs), .OpCode(OpCode[0]), .Enable(Branch), .Equal(branch_comparator_1_equal));
  not not_1 (not_1_out, OpCode[2]);
  and and_1 (jal, Jump, OpCode[0], OpCode[1], not_1_out);
  Multiplexer #(.width(8)) multiplexer_1 (
    .in0(PC_1), .in1(Immed), .out(multiplexer_1_out), .sel(branch_comparator_1_equal));  // open: en
  Multiplexer #(.select(3), .width(8)) multiplexer_2 (
    .in0(multiplexer_1_out), .in1(multiplexer_1_out), .in2(Rs[7:0]), .in3(Immed), .in4(Immed),
    .out(multiplexer_2_out), .sel(OpCode[2:0]));  // open: in5, in6, in7, en
  Multiplexer #(.width(8)) multiplexer_3 (
    .in0(PC_1), .in1(multiplexer_2_out), .out(Output), .sel(or_1_out));  // open: en
endmodule

module ALU_Source (
  input  func,
  input  [3:0] OpCode,
  input  [7:0] Immed,
  input  [3:0] Shamt,
  input  [15:0] Rt,
  output [15:0] Output
);

  wire [15:0] shift_1_shifted, signer_1_signed;

  Signer signer_1 (.Func(func), .Unsigned(Immed), .Signed(signer_1_signed));
  Shift shift_1 (.Reg_In(Rt), .Shamt(Shamt), .Shifted(shift_1_shifted), .func(func));
  Multiplexer #(.select(3), .width(16)) multiplexer_1 (
    .in1(Rt), .in2(signer_1_signed), .in3(Rt), .in4(shift_1_shifted), .out(Output), .sel(OpCode[2:0]));  // open: in0, in5, in6, in7, en
endmodule
